// Logisim project scheme.circ as structural Verilog: 16 circuits, main circuit datapath
module datapath (
  input  ram_wr_ctrl,
  input  [2:0] d_stack_shift,
  input  d_stack_wr,
  input  reg_ar_wr,
  input  reg_drw_wr,
  input  [2:0] r_stack_shift,
  input  r_stack_wr,
  input  [3:0] alu_ctrl,
  input  [6:0] alu_ctrl_pa,
  input  [6:0] alu_ctrl_pb,
  input  [2:0] demux_bus_c_reg_id_ctrl,
  input  alu_flag_ctrl,
  input  reg_ps_wr,
  input  [2:0] io_ctrl,
  input  reg_ip_wr,
  input  reg_cr_wr,
  input  [3:0] bus_X_in_ctrl,
  output iobus_clk,
  output [15:0] iobus_addr,
  output [31:0] iobus_data,
  output [2:0] iobus_ctrl
);

  wire clk, clk_wr;
  wire [3:0] alu_flag_out;
  wire [15:0] AR_q, bit_extender_1_out;
  wire [31:0] alu_a_in, alu_b_in, alu_X_in, and_1_out, bit_extender_2_out, bus_c, d_stack_in, d_stack_tos0,
       d_stack_tos1, DRW_q, io_ctrl_data_output, multiplexer_2_out, or_1_out, r_stack_in, r_stack_tos0,
       r_stack_tos1, ram_drr, reg_ar_in, reg_cr_in, reg_cr_out, reg_drw_in, reg_ip_in, reg_ip_out,
       reg_ps_out, register_1_q, register_2_q;

  Register #(.trigger("high"), .width(32)) register_1 (.D(alu_a_in), .clk(clk), .Q(register_1_q));  // open: en, clr
  Register #(.trigger("high"), .width(32)) register_2 (.D(alu_b_in), .clk(clk), .Q(register_2_q));  // open: en, clr
  ALU alu_1 (
    .porta(register_1_q), .portb(register_2_q), .operation(alu_ctrl), .porta_ctrl(alu_ctrl_pa),
    .portb_ctrl(alu_ctrl_pb), .bus_out(bus_c), .flags_out(alu_flag_out));
  Multiplexer #(.select(4), .width(32)) multiplexer_1 (
    .in0({32{1'b0}}), .in1(reg_ps_out), .in2(ram_drr), .in3(io_ctrl_data_output), .in4(d_stack_tos0),
    .in5(d_stack_tos1), .in6(r_stack_tos0), .in7(r_stack_tos1), .in8(reg_ip_out), .in9(reg_cr_out),
    .out(alu_X_in), .sel(bus_X_in_ctrl));  // open: in10, in11, in12, in13, in14, in15
  Demultiplexer #(.select(3), .width(32)) demultiplexer_1 (
    .out2(reg_drw_in), .out3(reg_ar_in), .out4(d_stack_in), .out5(r_stack_in), .out6(reg_ip_in),
    .out7(reg_cr_in), .in(bus_c), .sel(demux_bus_c_reg_id_ctrl));  // open: out0, out1
  Register #(.width(16)) AR (.D(bit_extender_1_out), .en(reg_ar_wr), .clk(reg_ar_wr), .Q(AR_q));  // open: clr
  Bit_Extender #(.in_width(32), .\type ("zero")) bit_extender_1 (.in(reg_ar_in), .out(bit_extender_1_out));
  Register #(.width(32)) DRW (.D(reg_drw_in), .en(reg_drw_wr), .clk(reg_drw_wr), .Q(DRW_q));  // open: clr
  assign and_1_out = reg_ps_out & ~32'hf;  // AND_Gate and_1, 32 bits wide
  assign bit_extender_2_out = {{28{1'b0}}, alu_flag_out};  // Bit_Extender bit_extender_2
  assign or_1_out = and_1_out | bit_extender_2_out;  // OR_Gate or_1, 32 bits wide
  Multiplexer #(.width(32)) multiplexer_2 (
    .in0(reg_ps_out), .in1(or_1_out), .out(multiplexer_2_out), .sel(alu_flag_ctrl));
  Register #(.width(32)) PS (.D(multiplexer_2_out), .en(reg_ps_wr), .clk(reg_ps_wr), .Q(reg_ps_out));  // open: clr
  Register #(.width(32)) IP (.D(reg_ip_in), .en(reg_ip_wr), .clk(reg_ip_wr), .Q(reg_ip_out));  // open: clr
  Register #(.width(32)) CR (.D(reg_cr_in), .en(reg_cr_wr), .clk(reg_cr_wr), .Q(reg_cr_out));  // open: clr
  memory memory_1 (.clk(clk), .wr(ram_wr_ctrl), .addr(AR_q), .in_data(DRW_q), .out_data(ram_drr));
  IOController iocontroller_1 (
    .clk(clk_wr), .data_in(bus_c), .ctrl(io_ctrl), .iobus_clk(iobus_clk), .iobus_addr(iobus_addr),
    .iobus_data(iobus_data), .iobus_ctrl(iobus_ctrl), .data_out(io_ctrl_data_output));
  Stack stack_1 (
    .clk(clk_wr), .shift_top(d_stack_shift), .wr_top(d_stack_wr), .data_in(d_stack_in), .tos0(d_stack_tos0),
    .tos1(d_stack_tos1));  // open: empty, full
  Stack stack_2 (
    .clk(clk_wr), .shift_top(r_stack_shift), .wr_top(r_stack_wr), .data_in(r_stack_in), .tos0(r_stack_tos0),
    .tos1(r_stack_tos1));  // open: empty, full
endmodule

module ALU (
  input  [31:0] porta,
  input  [31:0] portb,
  input  [3:0] operation,
  input  [6:0] porta_ctrl,
  input  [6:0] portb_ctrl,
  output [31:0] bus_out,
  output [3:0] flags_out
);
endmodule

module memory (
  input  clk,
  input  wr,
  input  [15:0] addr,
  input  [31:0] in_data,
  output [31:0] out_data
);
endmodule

module IOController (
  input  clk,
  input  [31:0] data_in,
  input  [2:0] ctrl,
  output iobus_clk,
  output [15:0] iobus_addr,
  output [31:0] iobus_data,
  output [2:0] iobus_ctrl,
  output [31:0] data_out
);
endmodule

module Stack (
  input  clk,
  input  [2:0] shift_top,
  input  wr_top,
  input  [31:0] data_in,
  output [31:0] tos0,
  output [31:0] tos1,
  output empty,
  output full
);
endmodule

module control (
  input  clk_dp,
  input  [63:0] control_bus,
  output alu_flag_ctrl,
  output reg_ps_wr,
  output ram_wr_ctrl,
  output [3:0] alu_ctrl,
  output [1:0] d_stack_shift,
  output [6:0] alu_ctrl_pa,
  output d_stack_wr,
  output reg_drw_wr,
  output [6:0] alu_ctrl_pb,
  output reg_ar_wr,
  output [3:0] mux_busa_in_ctrl,
  output [1:0] r_stack_shift,
  output reg_ip_wr,
  output reg_cr_wr,
  output [3:0] mux_busb_in_ctrl,
  output r_stack_wr,
  output [2:0] io_ctrl,
  output [2:0] demux_bus_c_reg_id_ctrl
);

  wire and_3_out, and_4_out, and_5_out, comparator_1_lt, reg_demux_reg_wr_q;

  and and_1 (d_stack_wr, control_bus[34], control_bus[0]);
  and and_2 (r_stack_wr, control_bus[34], control_bus[0]);
  Comparator #(.mode("unsigned"), .width(3)) comparator_1 (
    .a(3'b000), .b(control_bus[30:28]), .lt(comparator_1_lt));  // open: gt, eq
  and and_3 (and_3_out, control_bus[27], control_bus[0]);
  and and_4 (and_4_out, control_bus[31], control_bus[0]);
  and and_5 (and_5_out, control_bus[0], comparator_1_lt);
  Register #(.trigger("falling"), .width(1)) reg_reg_ps_wr (
    .D(and_3_out), .clk(clk_dp), .Q(reg_ps_wr));  // open: en, clr
  Register #(.trigger("falling"), .width(1)) reg_ram_wr (
    .D(and_4_out), .clk(clk_dp), .Q(ram_wr_ctrl));  // open: en, clr
  Register #(.trigger("falling"), .width(1)) reg_demux_reg_wr (
    .D(and_5_out), .clk(clk_dp), .Q(reg_demux_reg_wr_q));  // open: en, clr
  Register #(.trigger("falling"), .width(3)) reg_demux_id (
    .D(control_bus[30:28]), .clk(clk_dp), .Q(demux_bus_c_reg_id_ctrl));  // open: en, clr
  Demultiplexer #(.select(3)) demultiplexer_1 (
    .out2(reg_drw_wr), .out3(reg_ar_wr), .out6(reg_ip_wr), .out7(reg_cr_wr), .in(reg_demux_reg_wr_q),
    .sel(demux_bus_c_reg_id_ctrl));  // open: out0, out1, out4, out5

  assign alu_ctrl = control_bus[4:1];
  assign alu_ctrl_pa = control_bus[11:5];
  assign alu_ctrl_pb = control_bus[18:12];
  assign alu_flag_ctrl = control_bus[27];
  assign d_stack_shift = control_bus[33:32];
  assign io_ctrl = control_bus[41:39];
  assign mux_busa_in_ctrl = control_bus[22:19];
  assign mux_busb_in_ctrl = control_bus[26:23];
  assign r_stack_shift = control_bus[33:32];

  // Other names for the same wires on the sheet: is_exec_cmd = control_bus[0];
  //   bus_c_out_ctrl[2:0] = control_bus[30:28]; ram_ctrl = control_bus[31]; stack_d_ctrl[2:0] = control_bus[34:32];
  //   stack_r_ctrl[2:0] = control_bus[37:35]
endmodule

module dp_alu (
  input  clk,
  input  [3:0] alu_ctrl,
  input  [6:0] alu_ctrl_pa,
  input  [6:0] alu_ctrl_pb,
  input  [2:0] demux_bus_c_reg_id_ctrl
);

  wire [3:0] alu_flag_out;
  wire [31:0] alu_a_in, alu_b_in, bus_c, d_stack_in, r_stack_in, reg_ar_in, reg_cr_in, reg_drw_in, reg_ip_in,
       register_1_q, register_2_q;

  Register #(.trigger("high"), .width(32)) register_1 (.D(alu_a_in), .clk(clk), .Q(register_1_q));  // open: en, clr
  Register #(.trigger("high"), .width(32)) register_2 (.D(alu_b_in), .clk(clk), .Q(register_2_q));  // open: en, clr
  ALU alu_1 (
    .porta(register_1_q), .portb(register_2_q), .operation(alu_ctrl), .porta_ctrl(alu_ctrl_pa),
    .portb_ctrl(alu_ctrl_pb), .bus_out(bus_c), .flags_out(alu_flag_out));
  Demultiplexer #(.select(3), .width(32)) demultiplexer_1 (
    .out2(reg_drw_in), .out3(reg_ar_in), .out4(d_stack_in), .out5(r_stack_in), .out6(reg_ip_in),
    .out7(reg_cr_in), .in(bus_c), .sel(demux_bus_c_reg_id_ctrl));  // open: out0, out1
endmodule

module dp_mux (
  input  [3:0] bus_X_in_ctrl
);

  wire [31:0] alu_X_in, d_stack_tos0, d_stack_tos1, io_ctrl_data_output, r_stack_tos0, r_stack_tos1, ram_drr,
       reg_cr_out, reg_ip_out, reg_ps_out;

  Multiplexer #(.select(4), .width(32)) multiplexer_1 (
    .in0({32{1'b0}}), .in1(reg_ps_out), .in2(ram_drr), .in3(io_ctrl_data_output), .in4(d_stack_tos0),
    .in5(d_stack_tos1), .in6(r_stack_tos0), .in7(r_stack_tos1), .in8(reg_ip_out), .in9(reg_cr_out),
    .out(alu_X_in), .sel(bus_X_in_ctrl));  // open: in10, in11, in12, in13, in14, in15
endmodule

module dp_reg (
  input  alu_flag_ctrl,
  input  reg_ps_wr,
  input  reg_ip_wr,
  input  reg_cr_wr
);

  wire [3:0] alu_flag_out;
  wire [31:0] and_1_out, bit_extender_1_out, multiplexer_1_out, or_1_out, reg_cr_in, reg_cr_out, reg_ip_in,
       reg_ip_out, reg_ps_out;

  assign and_1_out = reg_ps_out & ~32'hf;  // AND_Gate and_1, 32 bits wide
  assign bit_extender_1_out = {{28{1'b0}}, alu_flag_out};  // Bit_Extender bit_extender_1
  Multiplexer #(.width(32)) multiplexer_1 (
    .in0(reg_ps_out), .in1(or_1_out), .out(multiplexer_1_out), .sel(alu_flag_ctrl));
  assign or_1_out = and_1_out | bit_extender_1_out;  // OR_Gate or_1, 32 bits wide
  Register #(.width(32)) PS (.D(multiplexer_1_out), .en(reg_ps_wr), .clk(reg_ps_wr), .Q(reg_ps_out));  // open: clr
  Register #(.width(32)) IP (.D(reg_ip_in), .en(reg_ip_wr), .clk(reg_ip_wr), .Q(reg_ip_out));  // open: clr
  Register #(.width(32)) CR (.D(reg_cr_in), .en(reg_cr_wr), .clk(reg_cr_wr), .Q(reg_cr_out));  // open: clr
endmodule

module dp_mem (
  input  ram_wr_ctrl,
  input  clk,
  input  clk_wr,
  input  [2:0] io_ctrl,
  input  reg_ar_wr,
  input  reg_drw_wr,
  output iobus_clk,
  output [15:0] iobus_addr,
  output [31:0] iobus_data,
  output [2:0] iobus_ctrl
);

  wire [15:0] AR_q, bit_extender_1_out;
  wire [31:0] bus_c, DRW_q, io_ctrl_data_output, ram_drr, reg_ar_in, reg_drw_in;

  Register #(.width(16)) AR (.D(bit_extender_1_out), .en(reg_ar_wr), .clk(reg_ar_wr), .Q(AR_q));  // open: clr
  Bit_Extender #(.in_width(32), .\type ("zero")) bit_extender_1 (.in(reg_ar_in), .out(bit_extender_1_out));
  Register #(.width(32)) DRW (.D(reg_drw_in), .en(reg_drw_wr), .clk(reg_drw_wr), .Q(DRW_q));  // open: clr
  memory memory_1 (.clk(clk), .wr(ram_wr_ctrl), .addr(AR_q), .in_data(DRW_q), .out_data(ram_drr));
  IOController iocontroller_1 (
    .clk(clk_wr), .data_in(bus_c), .ctrl(io_ctrl), .iobus_clk(iobus_clk), .iobus_addr(iobus_addr),
    .iobus_data(iobus_data), .iobus_ctrl(iobus_ctrl), .data_out(io_ctrl_data_output));
endmodule

module dp_stack (
  input  clk,
  input  [2:0] d_stack_shift,
  input  d_stack_wr,
  input  [2:0] r_stack_shift,
  input  r_stack_wr
);

  wire [31:0] d_stack_in, d_stack_tos0, d_stack_tos1, r_stack_in, r_stack_tos0, r_stack_tos1;

  Stack stack_1 (
    .clk(clk), .shift_top(d_stack_shift), .wr_top(d_stack_wr), .data_in(d_stack_in), .tos0(d_stack_tos0),
    .tos1(d_stack_tos1));  // open: empty, full
  Stack stack_2 (
    .clk(clk), .shift_top(r_stack_shift), .wr_top(r_stack_wr), .data_in(r_stack_in), .tos0(r_stack_tos0),
    .tos1(r_stack_tos1));  // open: empty, full
endmodule

module ctrl_in (
  input  [63:0] control_bus,
  output [3:0] alu_ctrl,
  output [6:0] alu_ctrl_pa,
  output [6:0] alu_ctrl_pb,
  output [3:0] mux_busa_in_ctrl,
  output [3:0] mux_busb_in_ctrl,
  output [2:0] io_ctrl
);

  wire is_exec_cmd;

  not not_1 (is_exec_cmd, control_bus[0]);

  assign alu_ctrl = control_bus[4:1];
  assign alu_ctrl_pa = control_bus[11:5];
  assign alu_ctrl_pb = control_bus[18:12];
  assign io_ctrl = control_bus[41:39];
  assign mux_busa_in_ctrl = control_bus[22:19];
  assign mux_busb_in_ctrl = control_bus[26:23];

  // Other names for the same wires on the sheet: alu_flag_ctrl = control_bus[27];
  //   bus_c_out_ctrl[2:0] = control_bus[30:28]; ram_ctrl = control_bus[31]; stack_d_ctrl[2:0] = control_bus[34:32];
  //   stack_r_ctrl[2:0] = control_bus[37:35]
endmodule

module ctrl_stack (
  output [1:0] d_stack_shift,
  output d_stack_wr,
  output [1:0] r_stack_shift,
  output r_stack_wr
);

  wire is_exec_cmd;
  wire [2:0] bit_extender_1_out, stack_d_ctrl;

  assign bit_extender_1_out = {{2{is_exec_cmd}}, is_exec_cmd};  // Bit_Extender bit_extender_1
  assign {d_stack_wr, d_stack_shift} = stack_d_ctrl & bit_extender_1_out;  // AND_Gate and_1, 3 bits wide
  assign {r_stack_wr, r_stack_shift} = bit_extender_1_out & stack_d_ctrl;  // AND_Gate and_2, 3 bits wide
endmodule

module ctrl_reg (
  input  clk_dp,
  output alu_flag_ctrl,
  output reg_ps_wr,
  output ram_wr_ctrl,
  output reg_drw_wr,
  output reg_ar_wr,
  output reg_ip_wr,
  output reg_cr_wr,
  output [2:0] demux_bus_c_reg_id_ctrl
);

  wire and_1_out, and_2_out, and_3_out, comparator_1_lt, is_exec_cmd, ram_ctrl, reg_demux_reg_wr_q;
  wire [2:0] bus_c_out_ctrl;

  Comparator #(.mode("unsigned"), .width(3)) comparator_1 (
    .a(3'b000), .b(bus_c_out_ctrl), .lt(comparator_1_lt));  // open: gt, eq
  and and_1 (and_1_out, alu_flag_ctrl, is_exec_cmd);
  and and_2 (and_2_out, ram_ctrl, is_exec_cmd);
  and and_3 (and_3_out, is_exec_cmd, comparator_1_lt);
  Register #(.trigger("falling"), .width(1)) reg_reg_ps_wr (
    .D(and_1_out), .clk(clk_dp), .Q(reg_ps_wr));  // open: en, clr
  Register #(.trigger("falling"), .width(1)) reg_ram_wr (
    .D(and_2_out), .clk(clk_dp), .Q(ram_wr_ctrl));  // open: en, clr
  Register #(.trigger("falling"), .width(1)) reg_demux_reg_wr (
    .D(and_3_out), .clk(clk_dp), .Q(reg_demux_reg_wr_q));  // open: en, clr
  Register #(.trigger("falling"), .width(3)) reg_demux_id (
    .D(bus_c_out_ctrl), .clk(clk_dp), .Q(demux_bus_c_reg_id_ctrl));  // open: en, clr
  Demultiplexer #(.select(3)) demultiplexer_1 (
    .out2(reg_drw_wr), .out3(reg_ar_wr), .out6(reg_ip_wr), .out7(reg_cr_wr), .in(reg_demux_reg_wr_q),
    .sel(demux_bus_c_reg_id_ctrl));  // open: out0, out1, out4, out5
endmodule

module ctrl_instr (
  input  clk,
  input  [31:0] bus_c,
  output [63:0] control_bus
);

  wire and_1_out, bitselector_1_out, xnor_1_out;
  wire [10:0] adder_1_out, multiplexer_1_out, reg_mc_pc_q;

  BitSelector #(.width(32)) bitselector_1 (.in(bus_c), .out(bitselector_1_out), .sel(control_bus[31:27]));
  Adder #(.width(11)) adder_1 (.a(reg_mc_pc_q), .b(11'h1), .out(adder_1_out));  // open: cin, cout
  xnor xnor_1 (xnor_1_out, bitselector_1_out, control_bus[32]);
  Multiplexer #(.width(11)) multiplexer_1 (
    .in0(adder_1_out), .in1(control_bus[43:33]), .out(multiplexer_1_out), .sel(and_1_out));
  and and_1 (and_1_out, control_bus[0], xnor_1_out);
  Register #(.trigger("falling"), .width(11)) reg_mc_pc (
    .D(multiplexer_1_out), .clk(clk), .Q(reg_mc_pc_q));  // open: en, clr
  mc_rom mc_rom_1 (.clk(clk), .addr(reg_mc_pc_q), .data(control_bus));

  // Other names for the same wires on the sheet: is_jmp = control_bus[0]; cmp_bit[4:0] = control_bus[31:27];
  //   cmp_val = control_bus[32]; cmp_jmp[10:0] = control_bus[43:33]
endmodule

module mc_rom (
  input  clk,
  input  [10:0] addr,
  output [63:0] data
);
endmodule
